# Fritzing sketch Circuit (saved by Fritzing 0.9.1b)
breadboards: 1

parts:
  Part2 = Arduino Nano (Rev3.0)
  SW1 = DIP Switch 8 Position [package=dipswitch-08]
  Speed_Control = POT [package=pot_mammoth]
  Volume = POT [package=pot_mammoth]
  U4 = 74HC595 [package="DIP16 [THT]"]
  LED2 = LED - 5mm [color="Red (633nm)" package="5 mm [THT]"]
  LED3 = LED - 5mm [color="Red (633nm)" package="5 mm [THT]"]
  LED4 = LED - 5mm [color="Red (633nm)" package="5 mm [THT]"]
  LED5 = LED - 5mm [color="Red (633nm)" package="5 mm [THT]"]
  LED6 = LED - 5mm [color="Red (633nm)" package="5 mm [THT]"]
  LED7 = LED - 5mm [color="Red (633nm)" package="5 mm [THT]"]
  LED8 = LED - 5mm [color="Red (633nm)" package="5 mm [THT]"]
  LED9 = LED - 5mm [color="Red (633nm)" package="5 mm [THT]"]
  R1 = Resistor [tolerance=±5% resistance=220 package=THT]
  R2 = Resistor [tolerance=±5% resistance=220 package=THT]
  R3 = Resistor [tolerance=±5% resistance=220 package=THT]
  R4 = Resistor [tolerance=±5% resistance=220 package=THT]
  R5 = Resistor [tolerance=±5% resistance=220 package=THT]
  R6 = Resistor [tolerance=±5% resistance=220 package=THT]
  R7 = Resistor [tolerance=±5% resistance=220 package=THT]
  R8 = Resistor [tolerance=±5% resistance=220 package=THT]
  Morse_Output = LED - 5mm [color="Red (633nm)" package="5 mm [THT]"]
  J1 = Piezo Speaker
  Power_plug1 = Power plug

nets:
  GND: Part2.GND, Speed_Control.S, Volume.S, U4.GND, U4.OE, LED2.anode, LED3.anode, LED4.anode, LED5.anode, LED6.anode, LED7.anode, LED8.anode, LED9.anode, Morse_Output.anode, J1.pin1, Power_plug1.GND
  N1: Part2.D2, U4.DS
  N2: Part2.D3, U4.ST_CP
  N3: Part2.D4, U4.SH_CP
  N4: Part2.D5, SW1.9
  N5: Part2.D6, SW1.10
  N6: Part2.D7, SW1.11
  N7: Part2.D8, SW1.12
  N8: Part2.D10, Volume.E
  VCC: Part2.VIN, SW1.1, SW1.2, SW1.3, SW1.4, SW1.5, SW1.6, SW1.7, SW1.8, Speed_Control.E, U4.MR, U4.VCC, Power_plug1.VCC
  N9: Part2.A7, Speed_Control.A
  N10: Part2.A3, SW1.13
  N11: Part2.A2, SW1.14
  N12: Part2.A1, SW1.15
  N13: Part2.A0, SW1.16
  N14: Part2.D13/SCK, Morse_Output.cathode
  N15: Volume.A, J1.pin2
  N16: U4.Q1, R8.Pin_1
  N17: U4.Q2, R4.Pin_1
  N18: U4.Q3, R6.Pin_1
  N19: U4.Q4, R5.Pin_1
  N20: U4.Q5, R3.Pin_1
  N21: U4.Q6, R2.Pin_1
  N22: U4.Q7, R1.Pin_1
  N23: U4.Q0, R7.Pin_1
  N24: LED2.cathode, R3.Pin_0
  N25: LED3.cathode, R5.Pin_0
  N26: LED4.cathode, R6.Pin_0
  N27: LED5.cathode, R4.Pin_0
  N28: LED6.cathode, R8.Pin_0
  N29: LED7.cathode, R7.Pin_0
  N30: LED8.cathode, R1.Pin_0
  N31: LED9.cathode, R2.Pin_0
